# Fritzing sketch DisplayForces (saved by Fritzing 0.6.3b)

parts:
  Arduino1 = Arduino
  Part1 = Triple_Axis_Accelerometer_Breakout___ADXL345

nets:
  N1: Arduino1.D3, Part1.connector17
  N2: Arduino1.D2, Part1.connector18
  N3: Arduino1.3V3, Part1.connector14
  N4: Arduino1.GND, Part1.connector15
  N5: Arduino1.A1, Part1.connector20
  N6: Arduino1.A2, Part1.connector21
  N7: Arduino1.A3, Part1.connector22
