# Fritzing sketch Sketch (saved by Fritzing 0.6.3b)
breadboards: 1

parts:
  U1 = 74HC595 [package="DIP16 [THT]"]
  Arduino1 = Arduino
  DI1 = 7-Segment LED Display [package=THT]

nets:
  N1: U1.Q1, DI1.cathodeDP
  GND: U1.GND, U1.OE, Arduino1.GND
  VCC: U1.MR, U1.VCC, Arduino1.+5V
  N2: U1.SH_CP, Arduino1.D12
  N3: U1.ST_CP, Arduino1.D8
  N4: U1.DS, Arduino1.D11
  N5: Arduino1.3V3, DI1.commAnode#2
